// Logisim project hkcpu.circ as structural Verilog
module alu (
  input  CLK,
  input  RST,
  input  [7:0] A,
  input  [7:0] B,
  input  [2:0] AOP,
  input  AO,
  output [2:0] FLGO,
  output [7:0] BUSO
);

  wire not_1_out;
  wire [2:0] comparator_1_gt;
  wire [7:0] adder_1_out, divider_1_out, multiplexer_1_out, multiplier_1_out, subtractor_1_out;

  Comparator comparator_1 (.a(A), .b(B), .gt(comparator_1_gt[0]), .eq(comparator_1_gt[1]), .lt(comparator_1_gt[2]));
  Adder adder_1 (.a(A), .b(B), .out(adder_1_out));  // open: cin, cout
  Subtractor subtractor_1 (.a(A), .b(B), .out(subtractor_1_out));  // open: bin, bout
  Multiplier multiplier_1 (.a(A), .b(B), .out(multiplier_1_out));  // open: cin, cout
  Divider divider_1 (.a(A), .b(B), .out(divider_1_out));  // open: upper, rem
  Register #(.width(3)) register_1 (.D(comparator_1_gt), .Q(FLGO), .clk(CLK), .clr(RST));  // open: en
  assign BUSO = AO ? multiplexer_1_out : 8'bz;  // Controlled_Buffer controlled_buffer_1
  Multiplexer #(.enable("true"), .select(2), .width(8)) multiplexer_1 (
    .in0(adder_1_out), .in1(subtractor_1_out), .in2(multiplier_1_out), .in3(divider_1_out),
    .out(multiplexer_1_out), .sel(AOP[1:0]), .en(not_1_out));
  not not_1 (not_1_out, AOP[2]);
endmodule
